# Fritzing sketch IoT-thermistor-pbs (saved by Fritzing 0.9.9b)
breadboards: 1

parts:
  Thermistor = Temperature Sensor (Thermistor) [thermistor_type=NTC package=THT]
  Resistor_(Thermistor) = Resistor [tolerance=±5% resistance=10k power=0.25 package=THT]
  Push-button_Switch_(PBS) = Pushbutton [package="[THT]"]
  Resistor_(PBS) = Resistor [tolerance=±5% resistance=220 package="2512 [SMD]"]
  Teensy_3_2 = Teensy 3.2  # not connected

nets:
  N1: Thermistor.pin_0, Resistor_(Thermistor).Pin_0
  N2: Thermistor.pin_1, Push-button_Switch_(PBS).Pin_3, Push-button_Switch_(PBS).Pin_4
  N3: Resistor_(Thermistor).Pin_1, Resistor_(PBS).Pin_1
  N4: Push-button_Switch_(PBS).Pin_1, Push-button_Switch_(PBS).Pin_2, Resistor_(PBS).Pin_0

notes:
  CST8227 - Interfacing
  Internet of Things (IoT)
  Thermistor with 10k-Ohm resistor connected to Pin A1 with push-button switch (PBS)
  in pull-down configuration.
  Pins
  1 (analog): thermistor
  3 (digital): push-button switch (PBS)
  Reference:
  Based on Tutorial #4 at PJRC.com (https://www.pjrc.com/teensy/tutorial4.html)
  Instructions:
  1) Build this circuit.
  2) Upload 'Standard Firmata Plus' to your Teensy; *quit* Arduino IDE and Teensy Loader.
  3) Run node-red
  Gerald.Hurdle@AlgonquinCollege.com

custom parts:
  Teensy 3.2: The Teensy is a complete USB-based microcontoller development system, in a very small footprint, capable of implementing many types of projects. All programming is done via the USB port. No special programmer is needed, only a standard micro-USB cable and a PC or Macintosh with a USB port. It has a USB keyboard/mouse/joystick emulation stack and can be programmed through Arduino IDE.
