# Fritzing sketch Sketch_For_Lab5 (saved by Fritzing 0.9.9b)
breadboards: 2

parts:
  R1 = Resistor [tolerance=±5% power=0.25 resistance=220 package=THT]
  R2 = Resistor [tolerance=±5% power=0.25 resistance=220 package=THT]
  R3 = Resistor [tolerance=±5% power=0.25 resistance=220 package=THT]
  R4 = Resistor [tolerance=±5% power=0.25 resistance=220 package=THT]
  R5 = Resistor [tolerance=±5% power=0.25 resistance=220 package=THT]
  R6 = Resistor [tolerance=±5% power=0.25 resistance=220 package=THT]
  R7 = Resistor [tolerance=±5% power=0.25 resistance=220 package=THT]
  R8 = Resistor [tolerance=±5% power=0.25 resistance=220 package=THT]
  R9 = Resistor [tolerance=±5% power=0.25 resistance=220 package=THT]
  R10 = Resistor [tolerance=±5% power=0.25 resistance=220 package=THT]
  R11 = Resistor [tolerance=±5% power=0.25 resistance=220 package=THT]
  R12 = Resistor [tolerance=±5% power=0.25 resistance=220 package=THT]
  R13 = Resistor [tolerance=±5% power=0.25 resistance=220 package=THT]
  R14 = Resistor [tolerance=±5% power=0.25 resistance=220 package=THT]
  R15 = Resistor [tolerance=±5% power=0.25 resistance=220 package=THT]
  R16 = Resistor [tolerance=±5% power=0.25 resistance=220 package=THT]
  Teensy_3_1 = Teensy 3.1  # not connected
  LED16 = LED - 3mm [color="Red (633nm)" current=0.030 package="3 mm [THT]"]
  LED17 = LED - 3mm [color="Red (633nm)" current=0.030 package="3 mm [THT]"]
  LED18 = LED - 3mm [color="Red (633nm)" current=0.030 package="3 mm [THT]"]
  LED19 = LED - 3mm [color="Red (633nm)" current=0.030 package="3 mm [THT]"]
  LED20 = LED - 3mm [color="Red (633nm)" current=0.030 package="3 mm [THT]"]
  LED21 = LED - 3mm [color="Red (633nm)" current=0.030 package="3 mm [THT]"]
  LED22 = LED - 3mm [color="Red (633nm)" current=0.030 package="3 mm [THT]"]
  LED23 = LED - 3mm [color="Red (633nm)" current=0.030 package="3 mm [THT]"]
  LED27 = LED - 3mm [color="Red (633nm)" current=0.030 package="3 mm [THT]"]
  LED28 = LED - 3mm [color="Red (633nm)" current=0.030 package="3 mm [THT]"]
  LED29 = LED - 3mm [color="Red (633nm)" current=0.030 package="3 mm [THT]"]
  LED30 = LED - 3mm [color="Red (633nm)" current=0.030 package="3 mm [THT]"]
  LED31 = LED - 3mm [color="Red (633nm)" current=0.030 package="3 mm [THT]"]
  LED32 = LED - 3mm [color="Red (633nm)" current=0.030 package="3 mm [THT]"]
  LED33 = LED - 3mm [color="Red (633nm)" current=0.030 package="3 mm [THT]"]
  LED34 = LED - 3mm [color="Red (633nm)" current=0.030 package="3 mm [THT]"]
  IC3 = H-Bridge [package=THT]
  IC4 = H-Bridge [package=THT]
  R17 = Resistor [tolerance=±5% power=0.25 resistance=220 package=THT]
  R18 = Resistor [tolerance=±5% power=0.25 resistance=220 package=THT]
  R19 = Resistor [tolerance=±5% power=0.25 resistance=220 package=THT]
  R20 = Resistor [tolerance=±5% power=0.25 resistance=220 package=THT]
  R21 = Resistor [tolerance=±5% power=0.25 resistance=220 package=THT]
  R22 = Resistor [tolerance=±5% power=0.25 resistance=220 package=THT]
  R23 = Resistor [tolerance=±5% power=0.25 resistance=220 package=THT]
  R24 = Resistor [tolerance=±5% power=0.25 resistance=220 package=THT]
  R25 = Resistor [tolerance=±5% power=0.25 resistance=220 package=THT]
  R26 = Resistor [tolerance=±5% power=0.25 resistance=220 package=THT]
  R27 = Resistor [tolerance=±5% power=0.25 resistance=220 package=THT]
  R28 = Resistor [tolerance=±5% power=0.25 resistance=220 package=THT]
  R29 = Resistor [tolerance=±5% power=0.25 resistance=220 package=THT]
  R30 = Resistor [tolerance=±5% power=0.25 resistance=220 package=THT]
  R31 = Resistor [tolerance=±5% power=0.25 resistance=220 package=THT]
  R32 = Resistor [tolerance=±5% power=0.25 resistance=220 package=THT]
  Teensy_3_2 = Teensy 3.1  # not connected
  IC5 = H-Bridge [package=THT]
  IC6 = H-Bridge [package=THT]
  DI1 = 7-Segment LED Display [package=THT]
  DI2 = 7-Segment LED Display [package=THT]

nets:
  N1: R1.Pin_0, LED33.anode
  N2: R1.Pin_1, IC3.2A
  N3: R2.Pin_0, LED32.anode
  N4: R2.Pin_1, IC3.2Y
  N5: R3.Pin_0, LED31.anode
  N6: R3.Pin_1, IC3.GND2
  N7: R4.Pin_0, LED30.anode
  N8: R4.Pin_1, IC3.GND1
  N9: R5.Pin_0, LED29.anode
  N10: R5.Pin_1, IC3.1Y
  N11: R6.Pin_0, LED27.anode
  N12: R6.Pin_1, IC3.1A
  N13: R7.Pin_0, LED17.anode
  N14: R7.Pin_1, IC4.1_2EN
  N15: R8.Pin_0, LED16.anode
  N16: R8.Pin_1, IC4.4A
  N17: R9.Pin_0, LED18.anode
  N18: R9.Pin_1, IC4.1A
  N19: R10.Pin_0, LED20.anode
  N20: R10.Pin_1, IC4.1Y
  N21: R11.Pin_0, LED21.anode
  N22: R11.Pin_1, IC4.GND1
  N23: R12.Pin_0, LED19.anode
  N24: R12.Pin_1, IC4.2Y
  N25: R13.Pin_0, LED34.anode
  N26: R13.Pin_1, IC3.4A
  N27: R14.Pin_0, LED28.anode
  N28: R14.Pin_1, IC3.1_2EN
  N29: R15.Pin_0, LED23.anode
  N30: R15.Pin_1, IC4.2A
  N31: R16.Pin_0, LED22.anode
  N32: R16.Pin_1, IC4.GND2
  GND4: LED16.cathode, LED17.cathode, LED18.cathode, LED19.cathode, LED20.cathode, LED21.cathode, LED22.cathode, LED23.cathode, LED27.cathode, LED28.cathode, LED29.cathode, LED30.cathode, LED31.cathode, LED32.cathode, LED33.cathode, LED34.cathode, IC3.GND4, IC4.VCC2, IC4.GND4
  N33: IC3.3_4EN, IC4.4Y
  N34: IC3.3A, IC3.VCC1, IC4.3A, IC4.VCC1
  N35: IC3.3Y, IC4.3Y
  GND3: IC3.GND3, IC4.GND3
  N36: R17.Pin_1, IC5.2Y
  N37: R18.Pin_0, DI2.cathodeB
  N38: R18.Pin_1, IC5.4A
  N39: R19.Pin_0, DI1.cathodeB
  N40: R19.Pin_1, IC6.1_2EN
  N41: R20.Pin_0, DI1.cathodeA
  N42: R20.Pin_1, IC6.4A
  N43: R21.Pin_1, IC5.2A
  N44: R22.Pin_0, DI2.cathodeG
  N45: R22.Pin_1, IC5.GND2
  N46: R23.Pin_0, DI2.cathodeF
  N47: R23.Pin_1, IC5.GND1
  N48: R24.Pin_0, DI2.cathodeE
  N49: R24.Pin_1, IC5.1Y
  N50: R25.Pin_0, DI2.cathodeC
  N51: R25.Pin_1, IC5.1_2EN
  N52: R26.Pin_0, DI2.cathodeD
  N53: R26.Pin_1, IC5.1A
  N54: R27.Pin_0, DI1.cathodeC
  N55: R27.Pin_1, IC6.1A
  N56: R28.Pin_0, DI1.cathodeD
  N57: R28.Pin_1, IC6.1Y
  N58: R29.Pin_0, DI1.cathodeE
  N59: R29.Pin_1, IC6.GND1
  N60: R30.Pin_0, DI1.cathodeF
  N61: R30.Pin_1, IC6.GND2
  N62: R31.Pin_0, DI1.cathodeG
  N63: R31.Pin_1, IC6.2Y
  N64: R32.Pin_0, DI2.cathodeA
  N65: R32.Pin_1, IC6.2A
  GND4_2: IC5.VCC2, IC5.GND4, IC6.VCC2, IC6.GND4
  N66: IC5.3A, IC5.VCC1, IC6.3A, IC6.VCC1, DI1.commAnode#2, DI2.commAnode#2
  N67: IC5.3Y, IC6.3Y
  GND3_2: IC5.GND3, IC6.GND3
  N68: IC5.4Y, IC6.3_4EN
