# Fritzing sketch Lab_6 (saved by Fritzing 0.9.9b)
breadboards: 1

parts:
  LED1 = RGB LED (com. cathode, rgb) [package="5 mm [THT]"]
  Resistor_(Green_LED) = Resistor [tolerance=±5% resistance=220 package="2512 [SMD]"]
  Resistor_(Blue_LED) = Resistor [tolerance=±5% resistance=220 package="2512 [SMD]"]
  Resistor_(Red_LED) = Resistor [tolerance=±5% resistance=220 package="2512 [SMD]"]
  Potentiometer = Trimmer Potentiometer [maximum_resistance=25kΩ package=THT]
  Teensy_3_2 = Teensy 3.2  # not connected
  R1 = Resistor [tolerance=±5% power=0.25 resistance=220 package=THT]
  R2 = Temperature Sensor (Thermistor) [thermistor_type=NTC package=THT]

nets:
  N1: LED1.red_anode, Resistor_(Red_LED).Pin_0
  N2: LED1.common_cathode, Resistor_(Blue_LED).Pin_0
  N3: LED1.green_anode, Potentiometer.leg1, R1.Pin_1
  N4: LED1.blue_anode, Resistor_(Green_LED).Pin_0
  N5: Potentiometer.leg2, R2.pin_0
  N6: R1.Pin_0, R2.pin_1

notes:
  Lab 6
  Yuliia Topalova

custom parts:
  Teensy 3.2: The Teensy is a complete USB-based microcontoller development system, in a very small footprint, capable of implementing many types of projects. All programming is done via the USB port. No special programmer is needed, only a standard micro-USB cable and a PC or Macintosh with a USB port. It has a USB keyboard/mouse/joystick emulation stack and can be programmed through Arduino IDE.
